# Fritzing sketch Hardware_v1_emitterCircuit (saved by Fritzing 0.9.3b)
perfboards: 1

parts:
  R1 = Resistor [tolerance=±5% resistance=120 package=THT]
  FET1 = MOSFET-NCHANNEL [package=to220v]
  +5V_Ctrl = Voltage Regulator - 5V [package="DPak [SMD]"]
  GND = BANANA_CONN [package=banana_conn]
  Cin = Ceramic Capacitor [capacitance=100nF package="100 mil [THT, multilayer]"]
  Cout = Ceramic Capacitor [capacitance=100nF package="100 mil [THT, multilayer]"]
  +24V = BANANA_CONN [package=banana_conn]
  ServoCon = Header 3 [package=molex-1x3_lock]
  +Motor = Header 2 [package=molex-1x2_lock]
  -Motor = Header 2 [package=molex-1x2_lock]
  ARduino = Arduino Nano (Rev3.0) (ICSP)

nets (from the breadboard view):
  N1: R1.Pin_0, ARduino.D9
  N2: R1.Pin_1, FET1.G
  N3: FET1.S, ServoCon.3, ARduino.D0/RX
  N4: +5V_Ctrl.input_voltage, Cin.1, +24V.1, +Motor.1
  N5: +5V_Ctrl.GND, Cin.0, Cout.0
  N6: +5V_Ctrl.output_voltage, Cout.1
  N7: GND.1, ARduino.GND
  N8: ServoCon.1, ARduino.D2
  N9: ServoCon.2, ARduino.VIN
  N10: -Motor.1, -Motor.2
