# Fritzing sketch Hardware_v2_Fullbridge (saved by Fritzing 0.9.3b)
circuit board: 18.8451cm x 10.2019cm
perfboards: 1

parts:
  R1 = Resistor [tolerance=±5% resistance=120 package=THT]
  GND = BANANA_CONN [package=banana_conn]
  Cin = Ceramic Capacitor [capacitance=100nF package="100 mil [THT, multilayer]"]
  Cout = Ceramic Capacitor [capacitance=100nF package="100 mil [THT, multilayer]"]
  +24V = BANANA_CONN [package=banana_conn]
  ServoCon = Header 3 [package=molex-1x3_lock]
  Arduino = Arduino Nano (Rev3.0)
  +Motor = Header 2 [package=molex-1x2_lock]
  -Motor = Header 2 [package=molex-1x2_lock]
  L+ = MOSFET-NCHANNEL [part_number=IRF1010N package=to220v]
  L- = MOSFET-NCHANNEL [part_number=IRF1010N package=to220v]
  C1 = Electrolytic Capacitor [capacitance=0.22mF package="100 mil [THT, electrolytic]"]
  C2 = Electrolytic Capacitor [capacitance=0.22mF package="100 mil [THT, electrolytic]"]
  R2 = Resistor [tolerance=±5% resistance=120 package=THT]
  R3 = Resistor [tolerance=±5% resistance=1k package=THT]
  R4 = Resistor [tolerance=±5% resistance=1k package=THT]
  H+ = Basic FET P-Channel [part_number=IRF5305 package="TO220 [THT]"]
  H- = Basic FET P-Channel [part_number=IRF5305 package="TO220 [THT]"]
  R5 = Resistor [tolerance=±5% resistance=4.7k package=THT]
  R6 = Resistor [tolerance=±5% resistance=4.7k package=THT]
  R7 = Resistor [tolerance=±5% resistance=15k package=THT]
  R8 = Resistor [tolerance=±5% resistance=15k package=THT]
  +5V_Ctrl = Voltage Regulator - 5V [package="TO220 [THT]"]
  NPN+ = NPN-Transistor [package="TO92 [THT]"]
  NPN- = NPN-Transistor [package="TO92 [THT]"]

nets:
  N1: R1.Pin_0, Arduino.D9
  N2: R1.Pin_1, L+.G, R7.Pin_0
  GND: GND.1, ServoCon.3, Arduino.GND, L+.S, L-.S, C2.-, R7.Pin_1, R8.Pin_1, NPN+.E, NPN-.E
  N3: Cin.0, Cout.0, +5V_Ctrl.GND
  24V: Cin.1, +24V.1, C1.+, H+.source, H-.source, R5.Pin_1, R6.Pin_1, +5V_Ctrl.input_voltage
  5V: Cout.1, ServoCon.2, Arduino.VIN, +5V_Ctrl.output_voltage
  N4: ServoCon.1, Arduino.D2
  N5: Arduino.D7, R3.Pin_0
  N6: Arduino.D8, R4.Pin_0
  N7: Arduino.D10, R2.Pin_0
  N8: +Motor.1, +Motor.2, L+.D, H+.drain
  N9: -Motor.1, -Motor.2, L-.D, H-.drain
  N10: L-.G, R2.Pin_1, R8.Pin_0
  N11: C1.-, C2.+
  N12: R3.Pin_1, NPN+.B
  N13: R4.Pin_1, NPN-.B
  N14: H+.gate, R5.Pin_0, NPN+.C
  N15: H-.gate, R6.Pin_0, NPN-.C
